// Logisim project CPU.circ as structural Verilog
module main (
  input  LOAD32
);

  wire control_1_fetch_from_pc_to_ir, control_1_fetch_operands1, control_1_increment_pc;
  wire [2:0] control_1_nextstate;
  wire [3:0] control_1_regaddr1_2, control_1_regaddr2_2, ir_dec_1_regaddr1, ir_dec_1_regaddr2,
       multiplexer_2_out;
  wire [4:0] ir_dec_1_opcode;
  wire [7:0] control_1_memaddr_2, ir_dec_1_memaddr;
  wire [15:0] inc_1_out_2, ir_dec_1_imm, mem_1_out_5, multiplexer_1_out, PC_q, reg_1_r0_2, reg_1_r1_2,
       reg_1_r2_2, reg_1_r3_2, reg_1_r4_2, reg_1_r5_2, reg_1_r6_2, reg_1_r7_2, reg_1_rbp_2, reg_1_rsp_2;
  wire [31:0] IR_q, rom_1_data;

  INC inc_1 (.in_1(PC_q), .out_2(inc_1_out_2));
  Register #(.width(16)) PC (.D(inc_1_out_2), .Q(PC_q), .clk(control_1_fetch_from_pc_to_ir));  // open: en, clr
  Register #(.width(32), .trigger("falling")) IR (
    .D(rom_1_data), .Q(IR_q), .clk(control_1_increment_pc));  // open: en, clr
  ROM #(.addrWidth(16), .dataWidth(32)) rom_1 (.addr(PC_q), .data(rom_1_data));  // open: sel
  IR_DEC ir_dec_1 (
    .in_1(IR_q), .OPCODE(ir_dec_1_opcode), .REGADDR1(ir_dec_1_regaddr1), .REGADDR2(ir_dec_1_regaddr2),
    .MEMADDR(ir_dec_1_memaddr), .IMM(ir_dec_1_imm));
  MEM mem_1 (.ADDR(control_1_memaddr_2), .LOAD(control_1_fetch_operands1), .out_5(mem_1_out_5));  // open: DATA, STORE
  REG reg_1 (
    .R0_2(reg_1_r0_2), .R1_2(reg_1_r1_2), .R2_2(reg_1_r2_2), .R3_2(reg_1_r3_2), .R4_2(reg_1_r4_2),
    .R5_2(reg_1_r5_2), .R6_2(reg_1_r6_2), .R7_2(reg_1_r7_2), .RSP_2(reg_1_rsp_2), .RBP_2(reg_1_rbp_2));  // open: R0, R1, R2, R3, R4, R5, R6, R7, RSP, RBP, REGADDR, CLK
  Multiplexer #(.select(4), .width(16)) multiplexer_1 (
    .in1(reg_1_r0_2), .in2(reg_1_r1_2), .in3(reg_1_r2_2), .in4(reg_1_r3_2), .in5(reg_1_r4_2),
    .in6(reg_1_r5_2), .in7(reg_1_r6_2), .in8(reg_1_r7_2), .in9(reg_1_rsp_2), .in10(reg_1_rbp_2),
    .out(multiplexer_1_out), .sel(multiplexer_2_out));  // open: in0, in11, in12, in13, in14, in15, en
  Multiplexer #(.width(4)) multiplexer_2 (
    .in0(control_1_regaddr1_2), .in1(control_1_regaddr2_2), .out(multiplexer_2_out),
    .sel(control_1_fetch_operands1));  // open: en
  CONTROL control_1 (
    .OPCODE(ir_dec_1_opcode), .REGADDR1(ir_dec_1_regaddr1), .MEMADDR(ir_dec_1_memaddr), .IMM(ir_dec_1_imm),
    .STATE(control_1_nextstate), .CLK(LOAD32), .REGADDR1_2(control_1_regaddr1_2),
    .MEMADDR_2(control_1_memaddr_2), .NEXTSTATE(control_1_nextstate),
    .Fetch_from_PC_to_IR(control_1_fetch_from_pc_to_ir), .Increment_PC(control_1_increment_pc),
    .Fetch_Operands1(control_1_fetch_operands1), .REGADDR2(ir_dec_1_regaddr2),
    .REGADDR2_2(control_1_regaddr2_2), .REG1(multiplexer_1_out), .REG2(multiplexer_1_out), .MEM(mem_1_out_5));  // open: OPCODE_2, IMM_2, Decode_Instruction, Execute_operation, Store_results, Repeat, Fetch_Operands2, REG1_2, REG2_2, MEM_2
  ALU alu_1 ();  // open: Data_1, Data_2, Control, OUTPUT

  // Notes on the sheet:
  //   contents of rom_1 (hex, n*v repeats v):
  //   1234
endmodule

module ALU (
  input  [15:0] Data_1,
  input  [15:0] Data_2,
  input  [3:0] Control,
  output [15:0] OUTPUT
);

  wire comparator_1_gt, comparator_1_lt;
  wire [15:0] adder_1_out, and_1_out, divider_1_out, divider_1_rem, multiplexer_1_out, multiplexer_2_out,
       multiplier_1_out, negator_1_out, not_1_out, or_1_out, subtractor_1_out, xor_1_out;

  Adder #(.width(16)) adder_1 (.a(Data_1), .b(Data_2), .out(adder_1_out));  // open: cin, cout
  Subtractor #(.width(16)) subtractor_1 (.a(Data_1), .b(Data_2), .out(subtractor_1_out));  // open: bin, bout
  Multiplier #(.width(16)) multiplier_1 (.a(Data_1), .b(Data_2), .out(multiplier_1_out));  // open: cin, cout
  Divider #(.width(16)) divider_1 (.a(Data_1), .b(Data_2), .out(divider_1_out), .rem(divider_1_rem));  // open: upper
  Negator #(.width(16)) negator_1 (.in(Data_1), .out(negator_1_out));
  Multiplexer #(.width(16)) multiplexer_1 (
    .in0(Data_1), .in1(Data_2), .out(multiplexer_1_out), .sel(comparator_1_lt));  // open: en
  Comparator #(.width(16)) comparator_1 (
    .a(Data_1), .b(Data_2), .gt(comparator_1_gt), .lt(comparator_1_lt));  // open: eq
  assign and_1_out = Data_1 & Data_2;  // AND_Gate and_1, 16 bits wide
  assign or_1_out = Data_1 | Data_2;  // OR_Gate or_1, 16 bits wide
  assign xor_1_out = Data_1 ^ Data_2;  // XOR_Gate xor_1, 16 bits wide
  assign not_1_out = ~Data_1;  // NOT_Gate not_1, 16 bits wide
  Multiplexer #(.width(16)) multiplexer_2 (
    .in0(Data_2), .in1(Data_1), .out(multiplexer_2_out), .sel(comparator_1_gt));  // open: en
  Multiplexer #(.select(4), .width(16)) multiplexer_3 (
    .in0(adder_1_out), .in1(subtractor_1_out), .in2(multiplier_1_out), .in3(divider_1_out),
    .in4(negator_1_out), .in5(divider_1_rem), .in6(multiplexer_1_out), .in7(multiplexer_2_out),
    .in8(and_1_out), .in9(or_1_out), .in10(xor_1_out), .in11(not_1_out), .out(OUTPUT), .sel(Control));  // open: in12, in13, in14, in15, en
endmodule

module IR_DEC (
  input  [31:0] in_1,
  output [4:0] OPCODE,
  output [3:0] REGADDR1,
  output [3:0] REGADDR2,
  output [7:0] MEMADDR,
  output [15:0] IMM
);


  assign IMM = in_1[24:9];
  assign MEMADDR = in_1[16:9];
  assign OPCODE = in_1[4:0];
  assign REGADDR1 = in_1[8:5];
  assign REGADDR2 = in_1[12:9];
endmodule

module CONTROL (
  input  [4:0] OPCODE,
  input  [3:0] REGADDR1,
  input  [3:0] REGADDR2,
  input  [7:0] MEMADDR,
  input  [15:0] IMM,
  input  [2:0] STATE,
  input  CLK,
  input  [15:0] REG1,
  input  [15:0] REG2,
  input  [15:0] MEM,
  output [4:0] OPCODE_2,
  output [3:0] REGADDR1_2,
  output [3:0] REGADDR2_2,
  output [7:0] MEMADDR_2,
  output [15:0] IMM_2,
  output [2:0] NEXTSTATE,
  output Fetch_from_PC_to_IR,
  output Increment_PC,
  output Decode_Instruction,
  output Fetch_Operands1,
  output Fetch_Operands2,
  output Execute_operation,
  output Store_results,
  output Repeat,
  output [15:0] REG1_2,
  output [15:0] REG2_2,
  output [15:0] MEM_2
);

  wire and_1_out, buff_1_out_2;
  wire [2:0] inc3_1_out_2, multiplexer_1_out, not_1_out;

  INC3 inc3_1 (.in_1(STATE), .out_2(inc3_1_out_2));
  assign not_1_out = ~3'b111;  // NOT_Gate not_1, 3 bits wide
  and and_1 (and_1_out, STATE[0], STATE[1], STATE[2]);
  Register #(.width(4), .trigger("falling")) REGADDR (
    .D(REGADDR1), .Q(REGADDR1_2), .clk(Decode_Instruction));  // open: en, clr
  Register #(.trigger("falling")) u_OPCODE (.D(MEMADDR), .Q(MEMADDR_2), .clk(Decode_Instruction));  // open: en, clr
  Multiplexer #(.width(3)) multiplexer_1 (
    .in0(inc3_1_out_2), .in1(not_1_out), .out(multiplexer_1_out), .sel(and_1_out));  // open: en
  Register #(.width(16), .trigger("falling")) u_REG1 (.D(REG1), .Q(REG1_2), .clk(Fetch_Operands1));  // open: en, clr
  Register #(.width(16), .trigger("falling")) u_REG2 (.D(REG2), .Q(REG2_2), .clk(Fetch_Operands2));  // open: en, clr
  Register #(.width(16)) u_MEM (.D(MEM), .Q(MEM_2), .clk(buff_1_out_2));  // open: en, clr
  Register #(.width(5), .trigger("falling")) u_OPCODE_2 (
    .D(OPCODE), .Q(OPCODE_2), .clk(Decode_Instruction));  // open: en, clr
  Register #(.width(4), .trigger("falling")) u_REGADDR2 (
    .D(REGADDR2), .Q(REGADDR2_2), .clk(Decode_Instruction));  // open: en, clr
  Register #(.width(16), .trigger("falling")) OPCODE_3 (.D(IMM), .Q(IMM_2), .clk(Decode_Instruction));  // open: en, clr
  Register #(.width(3)) u_STATE (.D(multiplexer_1_out), .Q(NEXTSTATE), .clk(CLK));  // open: en, clr
  Demultiplexer #(.select(3)) demultiplexer_1 (
    .out0(Fetch_from_PC_to_IR), .out1(Increment_PC), .out2(Decode_Instruction), .out3(Fetch_Operands1),
    .out4(Fetch_Operands2), .out5(Execute_operation), .out6(Store_results), .out7(Repeat), .in(1'b1),
    .sel(STATE));  // open: en
  BUFF buff_1 (.in_1(Fetch_Operands1), .out_2(buff_1_out_2));
endmodule

module REG (
  input  CLK,
  input  [3:0] REGADDR,
  input  [15:0] R0,
  input  [15:0] R1,
  input  [15:0] R2,
  input  [15:0] R3,
  input  [15:0] R4,
  input  [15:0] R5,
  input  [15:0] R6,
  input  [15:0] R7,
  input  [15:0] RSP,
  input  [15:0] RBP,
  output [15:0] R0_2,
  output [15:0] R1_2,
  output [15:0] R2_2,
  output [15:0] R3_2,
  output [15:0] R4_2,
  output [15:0] R5_2,
  output [15:0] R6_2,
  output [15:0] R7_2,
  output [15:0] RSP_2,
  output [15:0] RBP_2
);

  wire demultiplexer_1_out1, demultiplexer_1_out2, demultiplexer_1_out3, demultiplexer_1_out4,
       demultiplexer_1_out5, demultiplexer_1_out6, demultiplexer_1_out7, demultiplexer_1_out8,
       demultiplexer_1_out9, demultiplexer_1_out10;

  Demultiplexer #(.select(4)) demultiplexer_1 (
    .out1(demultiplexer_1_out1), .out2(demultiplexer_1_out2), .out3(demultiplexer_1_out3),
    .out4(demultiplexer_1_out4), .out5(demultiplexer_1_out5), .out6(demultiplexer_1_out6),
    .out7(demultiplexer_1_out7), .out8(demultiplexer_1_out8), .out9(demultiplexer_1_out9),
    .out10(demultiplexer_1_out10), .in(1'b1), .sel(REGADDR));  // open: out0, out11, out12, out13, out14, out15, en
  Register #(.width(16)) register_1 (.D(R0), .en(demultiplexer_1_out1), .Q(R0_2), .clk(CLK));  // open: clr
  Register #(.width(16)) register_2 (.D(R1), .en(demultiplexer_1_out2), .Q(R1_2), .clk(CLK));  // open: clr
  Register #(.width(16)) register_3 (.D(R2), .en(demultiplexer_1_out3), .Q(R2_2), .clk(CLK));  // open: clr
  Register #(.width(16)) register_4 (.D(R3), .en(demultiplexer_1_out4), .Q(R3_2), .clk(CLK));  // open: clr
  Register #(.width(16)) register_5 (.D(R4), .en(demultiplexer_1_out5), .Q(R4_2), .clk(CLK));  // open: clr
  Register #(.width(16)) register_6 (.D(R5), .en(demultiplexer_1_out6), .Q(R5_2), .clk(CLK));  // open: clr
  Register #(.width(16)) register_7 (.D(R6), .en(demultiplexer_1_out7), .Q(R6_2), .clk(CLK));  // open: clr
  Register #(.width(16)) register_8 (.D(R7), .en(demultiplexer_1_out8), .Q(R7_2), .clk(CLK));  // open: clr
  Register #(.width(16)) register_9 (.D(RSP), .en(demultiplexer_1_out9), .Q(RSP_2), .clk(CLK));  // open: clr
  Register #(.width(16)) register_10 (.D(RBP), .en(demultiplexer_1_out10), .Q(RBP_2), .clk(CLK));  // open: clr
endmodule

module MEM (
  input  [7:0] ADDR,
  input  [15:0] DATA,
  input  STORE,
  input  LOAD,
  output [15:0] out_5
);

  RAM #(.dataWidth(16), .bus("separate")) ram_1 (
    .addr(ADDR), .din(DATA), .data(out_5), .str(STORE), .clk(STORE), .ld(LOAD));  // open: sel, clr
endmodule

module INC (
  input  [15:0] in_1,
  output [15:0] out_2
);

  wire [15:0] bit_extender_1_out;

  assign bit_extender_1_out = {{15{1'b0}}, 1'b1};  // Bit_Extender bit_extender_1
  Adder #(.width(16)) adder_1 (.a(bit_extender_1_out), .b(in_1), .out(out_2));  // open: cin, cout
endmodule

module INC3 (
  input  [2:0] in_1,
  output [2:0] out_2
);

  wire [2:0] bit_extender_1_out;

  assign bit_extender_1_out = {{2{1'b0}}, 1'b1};  // Bit_Extender bit_extender_1
  Adder #(.width(3)) adder_1 (.a(bit_extender_1_out), .b(in_1), .out(out_2));  // open: cin, cout
endmodule

module INC8 (
  input  [7:0] in_1,
  output [7:0] out_2
);

  wire [7:0] bit_extender_1_out;

  assign bit_extender_1_out = {{7{1'b0}}, 1'b1};  // Bit_Extender bit_extender_1
  Adder adder_1 (.a(bit_extender_1_out), .b(in_1), .out(out_2));  // open: cin, cout
endmodule

module BUFF (
  input  in_1,
  output out_2
);

  wire buffer_1_out, buffer_2_out, buffer_3_out, buffer_4_out, buffer_5_out, buffer_6_out, buffer_7_out,
       buffer_8_out, buffer_9_out, buffer_10_out, buffer_11_out, buffer_12_out, buffer_13_out, buffer_14_out,
       buffer_15_out, buffer_16_out, buffer_17_out, buffer_18_out, buffer_19_out, buffer_20_out,
       buffer_21_out, buffer_22_out;

  buf buffer_1 (buffer_1_out, buffer_4_out);
  buf buffer_2 (buffer_2_out, in_1);
  buf buffer_3 (buffer_3_out, buffer_2_out);
  buf buffer_4 (buffer_4_out, buffer_3_out);
  buf buffer_5 (buffer_5_out, buffer_1_out);
  buf buffer_6 (buffer_6_out, buffer_7_out);
  buf buffer_7 (buffer_7_out, buffer_5_out);
  buf buffer_8 (buffer_8_out, buffer_6_out);
  buf buffer_9 (buffer_9_out, buffer_11_out);
  buf buffer_10 (buffer_10_out, buffer_9_out);
  buf buffer_11 (buffer_11_out, buffer_8_out);
  buf buffer_12 (buffer_12_out, buffer_10_out);
  buf buffer_13 (buffer_13_out, buffer_12_out);
  buf buffer_14 (buffer_14_out, buffer_13_out);
  buf buffer_15 (buffer_15_out, buffer_16_out);
  buf buffer_16 (buffer_16_out, buffer_14_out);
  buf buffer_17 (buffer_17_out, buffer_20_out);
  buf buffer_18 (buffer_18_out, buffer_17_out);
  buf buffer_19 (buffer_19_out, buffer_15_out);
  buf buffer_20 (buffer_20_out, buffer_19_out);
  buf buffer_21 (buffer_21_out, buffer_18_out);
  buf buffer_22 (buffer_22_out, buffer_21_out);
  buf buffer_23 (out_2, buffer_22_out);
endmodule
